# Fritzing sketch vertical_clock (saved by Fritzing 0.9.9b)
breadboards: 1

parts:
  Part1 = Arduino Nano (Rev3.0)
  U1 = Voltage Regulator [package=to220-adj]
  Rotary_Encoder1 = IDUINO Rotary Encoder SE055
  Power_plug1 = Power plug
  Part2 = DeadOn RTC - DS3234 Breakout

nets:
  GND: Part1.GND, U1.IN, Power_plug1.GND, Part2.GND
  N1: Part1.D2, Rotary_Encoder1.CLK
  VIN: Part1.VIN, U1.OUT, Part2.VCC
  N2: Part1.A5, Part2.SCL
  N3: Part1.A4, Part2.SDA
  N4: U1.ADJ, Power_plug1.VCC

custom parts:
  IDUINO Rotary Encoder SE055: https://www.conrad.com/p/iduino-rotary-encoder-1-pcs-se055-1485328
  DeadOn RTC - DS3234 Breakout: Description: Here is a real time clock based on the DS3234 Real Time Clock IC. The DS3234 is a low-cost, extremely accurate SPI bus real-time clock with an integrated temperature-compensated crystal oscillator and crystal. The RTC maintains seconds, minutes, hours, day, date, month, and year information. The date at the end of the month is automatically adjusted for months with fewer than 31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
