# Fritzing sketch vertical_clock_breadboard (saved by Fritzing 0.9.9b)
circuit board: 7.67839cm x 10.1219cm
circuit board: 8.85467cm x 13.762cm
breadboards: 2

parts:
  Part1 = Arduino Nano (Rev3.0)
  Power_plug1 = Power plug
  Part2 = DeadOn RTC - DS3234 Breakout
  LED1 = LED - 5mm [color="White (4500K)" current=0.030 package="5 mm [THT]"]
  Q1 = NPN-Transistor [package="TO92 [THT]"]
  R1 = Resistor [tolerance=±5% power=0.25 resistance=1k package=THT]
  LED2 = LED - 5mm [color="White (4500K)" current=0.030 package="5 mm [THT]"]
  R2 = Resistor [tolerance=±5% power=0.25 resistance=1k package=THT]
  Pololu_A1 = Pololu A4988 [package=SO16]
  Pololu_A2 = Pololu A4988 [package=SO16]
  Pololu_A3 = Pololu A4988 [package=SO16]
  M5 = Stepper Motor - Bipolar
  M6 = Stepper Motor - Bipolar
  M8 = Stepper Motor - Bipolar
  Q2 = NPN-Transistor [package="TO92 [THT]"]
  J1 = Screw terminal - 2 pins [package=THT]
  J2 = Screw terminal - 2 pins [package=THT]
  Pololu_A4 = Pololu A4988 [package=SO16]
  M7 = Stepper Motor - Bipolar
  Rotary_Encoder1 = IDUINO Rotary Encoder SE055
  J4 = Screw terminal - 2 pins [package=THT]
  R3 = Resistor [tolerance=±5% power=0.25 resistance=1k package=THT]
  R5 = Resistor [tolerance=±5% power=0.25 resistance=220 package=THT]

nets:
  GND: Part1.GND, Power_plug1.GND, Part2.GND, Q1.E, Pololu_A1.GND, Pololu_A2.GND, Pololu_A3.GND, Q2.E, J1.pin1, J2.pin1, Pololu_A4.GND, Rotary_Encoder1.GND, J4.pin1
  N1: Part1.D2, Rotary_Encoder1.SW
  N2: Part1.D3, Rotary_Encoder1.CLK
  N3: Part1.D4, Rotary_Encoder1.DT
  N4: Part1.D5, Pololu_A4.DIR
  N5: Part1.D6, Pololu_A4.STEP
  N6: Part1.D7, Pololu_A1.DIR
  N7: Part1.D8, Pololu_A1.STEP
  N8: Part1.D9, Pololu_A3.DIR
  N9: Part1.D10, Pololu_A3.STEP
  N10: Part1.D11/MOSI, Pololu_A2.DIR
  N11: Part1.D12/MISO, Pololu_A2.STEP
  VIN: Part1.VIN, Power_plug1.VCC, R1.Pin_0, R2.Pin_0
  5V: Part1.5V, Part2.VCC, Pololu_A1.VMOT, Pololu_A2.VMOT, Pololu_A3.VMOT, J2.pin2, Pololu_A4.VMOT, Rotary_Encoder1.VDD, J4.pin2
  N12: Part1.A7, R5.Pin_0
  N13: Part1.A6, R3.Pin_0
  N14: Part1.A5, Part2.SCL
  N15: Part1.A4, Part2.SDA
  N16: Part1.D13/SCK, Pololu_A1.ENABLE, Pololu_A2.ENABLE, Pololu_A3.ENABLE, Pololu_A4.ENABLE
  N17: LED1.cathode, Q1.C
  N18: LED1.anode, R1.Pin_1
  N19: Q1.B, R3.Pin_1
  N20: LED2.cathode, Q2.C
  N21: LED2.anode, R2.Pin_1
  N22: Pololu_A1.RESET, Pololu_A1.SLEEP
  VDD: Pololu_A1.VDD, Pololu_A2.VDD, Pololu_A3.VDD, J1.pin2, Pololu_A4.VDD
  N23: Pololu_A1.1B, M7.D
  N24: Pololu_A1.1A, M7.B
  N25: Pololu_A1.2A, M7.C
  N26: Pololu_A1.2B, M7.A
  N27: Pololu_A2.RESET, Pololu_A2.SLEEP
  N28: Pololu_A2.1B, M6.D
  N29: Pololu_A2.1A, M6.B
  N30: Pololu_A2.2A, M6.C
  N31: Pololu_A2.2B, M6.A
  N32: Pololu_A3.RESET, Pololu_A3.SLEEP
  N33: Pololu_A3.1B, M8.D
  N34: Pololu_A3.1A, M8.B
  N35: Pololu_A3.2A, M8.C
  N36: Pololu_A3.2B, M8.A
  N37: M5.A, Pololu_A4.2B
  N38: M5.C, Pololu_A4.2A
  N39: M5.B, Pololu_A4.1A
  N40: M5.D, Pololu_A4.1B
  N41: Q2.B, R5.Pin_1
  N42: Pololu_A4.RESET, Pololu_A4.SLEEP

custom parts:
  DeadOn RTC - DS3234 Breakout: Description: Here is a real time clock based on the DS3234 Real Time Clock IC. The DS3234 is a low-cost, extremely accurate SPI bus real-time clock with an integrated temperature-compensated crystal oscillator and crystal. The RTC maintains seconds, minutes, hours, day, date, month, and year information. The date at the end of the month is automatically adjusted for months with fewer than 31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
  IDUINO Rotary Encoder SE055: https://www.conrad.com/p/iduino-rotary-encoder-1-pcs-se055-1485328
