# Fritzing sketch vertical_clock_prototype_board (saved by Fritzing 0.9.9b)
circuit board: 8.85467cm x 13.762cm
circuit board: 7.67839cm x 10.1219cm
perfboards: 2

parts:
  Part1 = Arduino Nano (Rev3.0)
  Power_plug1 = Power plug
  Part2 = DeadOn RTC - DS3234 Breakout
  Q1 = NPN-Transistor [package="TO92 [THT]"]
  R1 = Resistor [tolerance=±5% power=0.25 resistance=1k package=THT]
  R2 = Resistor [tolerance=±5% power=0.25 resistance=1k package=THT]
  Pololu_A1 = Pololu A4988 [package=SO16]
  Pololu_A2 = Pololu A4988 [package=SO16]
  Pololu_A3 = Pololu A4988 [package=SO16]
  Q2 = NPN-Transistor [package="TO92 [THT]"]
  Pololu_A4 = Pololu A4988 [package=SO16]
  LED1 = LED - 3mm [color="White (4500K)" current=0.030 package="3 mm [THT]"]
  LED2 = LED - 3mm [color="White (4500K)" current=0.030 package="3 mm [THT]"]
  C1 = Capacitor Polarized [package=cpol-radial-100uf-25v]
  C2 = Capacitor Polarized [package=cpol-radial-100uf-25v]
  C3 = Capacitor Polarized [package=cpol-radial-100uf-25v]
  C4 = Capacitor Polarized [package=cpol-radial-100uf-25v]
  Rotary_Encoder2 = IDUINO Rotary Encoder SE055
  J8 = double row female pin header, 2 pins [form="♀ (female)"]
  J9 = female pin header, 10 pins [form="♀ (female)"]
  J4 = female pin header, 4 pins [form="♀ (female)"]
  J2 = female pin header, 10 pins [form="♀ (female)"]
  J10 = female pin header, 4 pins [form="♀ (female)"]
  J16 = male pin header, 5 pins [form="♂ (male)"]
  J17 = female pin header, 4 pins [form="♀ (female)"]
  J18 = female pin header, 4 pins [form="♀ (female)"]
  J19 = female pin header, 4 pins [form="♀ (female)"]
  J20 = female pin header, 4 pins [form="♀ (female)"]
  R3 = Resistor [tolerance=±5% power=0.25 resistance=1k package=THT]
  R4 = Resistor [tolerance=±5% power=0.25 resistance=1k package=THT]

nets:
  GND: Part1.GND, Power_plug1.GND, Part2.GND, Q1.C, Q2.C, Pololu_A4.GND#8, Rotary_Encoder2.GND, J8.pin1, J4.pin2
  N1: Part1.D2, Rotary_Encoder2.SW, J16.pin4
  N2: Part1.D3, Rotary_Encoder2.CLK, J16.pin3
  N3: Part1.D4, Rotary_Encoder2.DT, J16.pin2
  N4: Part1.D5, Pololu_A4.DIR, J9.pin9, J2.pin9
  N5: Part1.D6, Pololu_A4.STEP, J9.pin8, J2.pin8
  N6: Part1.D7, Pololu_A1.DIR, J9.pin7, J2.pin7
  N7: Part1.D8, Pololu_A1.STEP, J9.pin6, J2.pin6
  N8: Part1.D9, Pololu_A3.DIR, J9.pin5, J2.pin5
  N9: Part1.D10, Pololu_A3.STEP, J9.pin4, J2.pin4
  N10: Part1.D11/MOSI, Pololu_A2.DIR, J9.pin3, J2.pin3
  N11: Part1.D12/MISO, Pololu_A2.STEP, J9.pin2, J2.pin2
  VIN: Part1.VIN, Power_plug1.VCC, R1.Pin_0, R2.Pin_0, Pololu_A1.VMOT, Pololu_A2.VMOT, Pololu_A3.VMOT, Pololu_A4.VMOT, C1.-, C2.-, C3.-, C4.-, J8.pin2, J4.pin3, J10.pin2
  5V: Part1.5V, Part2.VCC
  N12: Part1.A5, Part2.SCL
  N13: Part1.A4, Part2.SDA
  N14: Part1.A2, R4.Pin_0
  N15: Part1.D13/SCK, Pololu_A1.ENABLE, Pololu_A2.ENABLE, Pololu_A3.ENABLE, Pololu_A4.ENABLE, J9.pin1, J2.pin1
  N16: Q1.E, LED1.cathode
  N17: Q1.B, R3.Pin_1
  N18: R1.Pin_1, LED1.anode
  N19: R2.Pin_1, LED2.anode
  N20: Pololu_A1.RESET, Pololu_A1.SLEEP
  VDD: Pololu_A1.VDD, Pololu_A2.VDD, Pololu_A3.VDD, Rotary_Encoder2.VDD, J4.pin1, J10.pin4
  N21: Pololu_A1.1B, J19.pin4
  N22: Pololu_A1.1A, J19.pin3
  N23: Pololu_A1.2A, J19.pin2
  N24: Pololu_A1.2B, J19.pin1
  N25: Pololu_A1.GND#14, C1.+
  N26: Pololu_A2.RESET, Pololu_A2.SLEEP
  N27: Pololu_A2.GND#8, Pololu_A3.GND#8, J10.pin3
  N28: Pololu_A2.1A, J17.pin3
  N29: Pololu_A2.2A, J17.pin2
  N30: Pololu_A2.2B, J17.pin1
  N31: Pololu_A2.GND#14, C2.+
  N32: Pololu_A3.RESET, Pololu_A3.SLEEP
  N33: Pololu_A3.1B, J20.pin4
  N34: Pololu_A3.1A, J20.pin3
  N35: Pololu_A3.2A, J20.pin2
  N36: Pololu_A3.2B, J20.pin1
  N37: Pololu_A3.GND#14, C4.+
  N38: Q2.E, LED2.cathode
  N39: Q2.B, R4.Pin_1
  N40: Pololu_A4.RESET, Pololu_A4.SLEEP
  N41: Pololu_A4.1B, J18.pin4
  N42: Pololu_A4.1A, J18.pin3
  N43: Pololu_A4.2A, J18.pin2
  N44: Pololu_A4.2B, J18.pin1
  N45: Pololu_A4.GND#14, C3.+

custom parts:
  DeadOn RTC - DS3234 Breakout: Description: Here is a real time clock based on the DS3234 Real Time Clock IC. The DS3234 is a low-cost, extremely accurate SPI bus real-time clock with an integrated temperature-compensated crystal oscillator and crystal. The RTC maintains seconds, minutes, hours, day, date, month, and year information. The date at the end of the month is automatically adjusted for months with fewer than 31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
  IDUINO Rotary Encoder SE055: https://www.conrad.com/p/iduino-rotary-encoder-1-pcs-se055-1485328
